# Fritzing sketch xmas.atmega328 (saved by Fritzing 0.9.3b)
circuit board: 4.2cm x 6.45cm
breadboards: 1

parts:
  MC1 = atmega328 [package=dip]
  XTAL1 = Crystal [frequency="16 Mhz" package=THT]
  R1 = Resistor [tolerance=±5% resistance=10k package=THT]
  C1 = Electrolytic Capacitor [capacitance=1mF voltage=16V package="100 mil [THT, electrolytic]"]
  C2 = Ceramic Capacitor [capacitance=22pF voltage=50V package="100 mil [THT, multilayer]"]
  C3 = Ceramic Capacitor [capacitance=22pF voltage=50V package="100 mil [THT, multilayer]"]
  R2 = Resistor [tolerance=±5% resistance=330 package=THT]
  R3 = Resistor [tolerance=±5% resistance=10k package=THT]
  PWR = LED - 5mm [color="Red (633nm)" package="5 mm [THT]"]
  R4 = Resistor [tolerance=±5% resistance=220 package=THT]
  J5 = female pin header, 6 pins [form="♀ (female)"]
  C4 = Ceramic Capacitor [capacitance=100nF package="100 mil [THT, multilayer]"]
  J4 = screw terminal, 3 pins
  J3 = screw terminal, 2 pins
  S2 = Pushbutton [package="[THT]"]

nets:
  N1: MC1.RESET, R1.Pin_1, C4.1
  N2: MC1.D0_(RX), J5.pin4
  N3: MC1.D1_(TX), J5.pin5
  N4: MC1.D2, R3.Pin_1, S2.Pin_3, S2.Pin_4
  N5: MC1.VCC, MC1.AVCC, R1.Pin_0, C1.+, PWR.anode, J5.pin3, J4.pin3, J3.pin2, S2.Pin_1, S2.Pin_2
  N6: MC1.GND, C1.-, C2.0, C3.1, R3.Pin_0, R4.Pin_0, J5.pin1, J4.pin1, J3.pin1
  N7: MC1.XLAT1, XTAL1.pin_0, C2.1
  N8: MC1.XLAT2, XTAL1.pin_1, C3.0
  N9: MC1.D7, R2.Pin_0
  N10: R2.Pin_1, J4.pin2
  N11: PWR.cathode, R4.Pin_1
  N12: J5.pin6, C4.0

notes:
  Xmas2019
  v1908-5
  GND
  CTL
  V+
  VCC
  TX
  RX
  DTR

custom parts:
  Pushbutton: A generic pushbutton.
