# Fritzing sketch xmas (saved by Fritzing 0.9.3b)
breadboards: 1

parts:
  C1 = Electrolytic Capacitor [capacitance=1mF voltage=16V package="100 mil [THT, electrolytic]"]
  Arduino_Nano = Arduino Nano (Rev3.0) (ICSP)
  5V_10A = Power plug
  LED-Strip_Connector = Camdenboss CTB0158-3 [part_number=CTB0158-3 package=THT]
  R2 = Resistor [tolerance=±5% resistance=10k package=THT]
  S1 = Momentary Switch [package=tactile-pth]
  R1 = Resistor [tolerance=±5% resistance=330 package=THT]

nets:
  GND: C1.-, Arduino_Nano.GND, 5V_10A.GND, LED-Strip_Connector.pin1, R2.Pin_1, S1.2
  VIN: C1.+, Arduino_Nano.VIN, 5V_10A.VCC, LED-Strip_Connector.pin3, S1.3
  N1: Arduino_Nano.D2, R2.Pin_0
  N2: Arduino_Nano.D7, R1.Pin_0
  N3: LED-Strip_Connector.pin2, R1.Pin_1

notes:
  Xmas 2019, LED-Strip Controller, 5
